# Fritzing sketch datalogger Sketch (saved by Fritzing 0.9.9b)
circuit board: 13.1328cm x 9.44503cm

parts:
  o1 = Module display OLED I2C 128x64 SSD1306 [package=THT]
  microSD1 = MicroSD Card Module
  ZS-042_RTC1 = ZS-042 RTC Module
  U1 = MAX6675 [package=so08]
  M1 = MT3608_Module
  S3 = Pushbutton [package="[THT]"]
  S4 = Pushbutton [package="[THT]"]
  MCU1 = Wemos Lolin32lite
  U5 = MAX6675 [package=so08]
  J1 = Screw terminal - 2 pins [package=THT]
  J2 = Screw terminal - 2 pins [package=THT]
  J3 = Screw terminal - 2 pins [package=THT]
  U4 = MAX6675 [package=so08]

nets:
  GND: o1.GND, microSD1.GND, ZS-042_RTC1.GND, U1.VSS, M1.connector3, U5.VSS, U4.VSS
  VCC: o1.VCC, microSD1.VCC, ZS-042_RTC1.VCC, U1.VDD, M1.connector2, U5.VDD, U4.VDD
  N1: o1.SCL, ZS-042_RTC1.SCL, MCU1.pin_5, MCU1.pin_6
  N2: o1.SDA, ZS-042_RTC1.SDA, MCU1.pin_7
  N3: microSD1.MISO, MCU1.pin_26
  N4: microSD1.MOSI, microSD1.SCK, MCU1.pin_24, MCU1.pin_25
  N5: microSD1.CS, MCU1.pin_23
  N6: U1.T-, J3.pin2
  N7: U1.T+, J3.pin1
  N8: U1.SCK, MCU1.pin_19, MCU1.pin_20, MCU1.pin_21, U5.SCK, U5.CS, U4.SCK
  N9: U1.CS, MCU1.pin_16
  N10: U1.MISO, MCU1.pin_22, U5.MISO, U4.MISO
  N11: M1.connector0, S3.Pin_3, S3.Pin_4, S4.Pin_3, S4.Pin_4, MCU1.pin_2, MCU1.pin_8, MCU1.pin_9, MCU1.pin_10, MCU1.pin_13
  N12: M1.connector1, MCU1.pin_27, MCU1.pin_28
  N13: MCU1.pin_17, U4.CS
  N14: U5.T-, J1.pin2
  N15: U5.T+, J1.pin1
  N16: J2.pin1, U4.T+
  N17: J2.pin2, U4.T-

custom parts:
  Module display OLED I2C 128x64 SSD1306: Ecran OLED I2C SSD163 de 128x64 avec connexion I2C
  Wemos Lolin32lite: Wemos Lolinlite32 wifi and blue tooth board based on the ESP-32 cpu, digital I/Os 19, analog inputs 6, clock 240mhz, Flash 4Mbytes, lipo battery charger (500ma connection broken out on breadboard but not pcb), usb.
